// Logisim project 25SP-007-CS(HAFSA FAIZEE).circ as structural Verilog: 5 circuits, main circuit main
module main (
  input  in_1,
  input  in_2
);

  wire clock_1_out, decoder_1_out0, decoder_1_out1, decoder_1_out2, decoder_1_out3, not_1_out, xor_1_out;
  wire [1:0] register_1_q;
  wire [2:0] rom_1_data;
  wire [3:0] adder_2_out, and_1_out, multiplexer_1_out, multiplexer_2_out, multiplexer_3_out,
       multiplexer_4_out, not_2_out, or_1_out, register_2_q, register_3_q, register_4_q, register_5_q,
       rom_1_data_3, subtractor_1_out, xor_2_out;
  wire [7:3] rom_1_data_2;
  wire [9:0] register_1_q_2;
  wire [11:0] adder_1_out;

  not not_1 (not_1_out, rom_1_data_2[3]);
  ROM #(.addrWidth(10), .dataWidth(12)) rom_1 (
    .addr(register_1_q_2), .data({rom_1_data_3, rom_1_data_2, rom_1_data}), .sel(in_1));
  Register #(.width(12)) register_1 (
    .D(adder_1_out), .en(in_1), .Q({register_1_q_2, register_1_q}), .clk(clock_1_out), .clr(in_2));
  Adder #(.width(12)) adder_1 (.a({register_1_q_2, register_1_q}), .b(12'h4), .out(adder_1_out));  // open: cin, cout
  Clock clock_1 (.out(clock_1_out));
  xor xor_1 (xor_1_out, rom_1_data_2[3], not_1_out);
  Decoder #(.select(2)) decoder_1 (
    .out0(decoder_1_out0), .out1(decoder_1_out1), .out2(decoder_1_out2), .out3(decoder_1_out3),
    .sel(rom_1_data_2[5:4]), .en(xor_1_out));
  Register #(.width(4)) register_2 (.D(4'b0000), .en(decoder_1_out0), .Q(register_2_q));  // open: clk, clr
  Register #(.width(4)) register_3 (
    .D(multiplexer_4_out), .en(decoder_1_out1), .Q(register_3_q), .clk(clock_1_out));  // open: clr
  Register #(.width(4)) register_4 (
    .D(multiplexer_4_out), .en(decoder_1_out2), .Q(register_4_q), .clk(clock_1_out));  // open: clr
  Register #(.width(4)) register_5 (
    .D(multiplexer_4_out), .en(decoder_1_out3), .Q(register_5_q), .clk(clock_1_out));  // open: clr
  Multiplexer #(.select(2), .width(4), .enable("false")) multiplexer_1 (
    .in0(register_2_q), .in1(register_3_q), .in2(register_4_q), .in3(register_5_q), .out(multiplexer_1_out),
    .sel(rom_1_data_2[7:6]));
  Multiplexer #(.select(2), .width(4), .enable("false")) multiplexer_2 (
    .in0(register_2_q), .in1(register_3_q), .in2(register_4_q), .in3(register_5_q), .out(multiplexer_2_out),
    .sel(rom_1_data_3[1:0]));
  Multiplexer #(.width(4), .enable("false")) multiplexer_3 (
    .in0(multiplexer_2_out), .in1(rom_1_data_3), .out(multiplexer_3_out), .sel(rom_1_data_2[3]));
  Adder #(.width(4)) adder_2 (.a(multiplexer_1_out), .b(multiplexer_3_out), .out(adder_2_out));  // open: cin, cout
  Subtractor #(.width(4)) subtractor_1 (
    .a(multiplexer_1_out), .b(multiplexer_3_out), .out(subtractor_1_out));  // open: bin, bout
  assign and_1_out = multiplexer_1_out & multiplexer_3_out;  // AND_Gate and_1, 4 bits wide
  assign or_1_out = multiplexer_1_out | multiplexer_3_out;  // OR_Gate or_1, 4 bits wide
  assign xor_2_out = multiplexer_1_out ^ multiplexer_3_out;  // XOR_Gate xor_2, 4 bits wide
  assign not_2_out = ~multiplexer_1_out;  // NOT_Gate not_2, 4 bits wide
  Multiplexer #(.select(3), .width(4), .enable("false")) multiplexer_4 (
    .in0(adder_2_out), .in1(subtractor_1_out), .in2(and_1_out), .in3(or_1_out), .in4(xor_2_out),
    .in5(not_2_out), .out(multiplexer_4_out), .sel(rom_1_data));  // open: in6, in7

  // Notes on the sheet:
  //   Hafsa Faizee
  //   25sp-007-cs
  //   contents of rom_1 (hex, n*v repeats v):
  //   518 328 270 2d1 1e2 273 d5 f6c
  //   rs1
  //   rs2
endmodule

module register_file (
  input  [3:0] data,
  input  [3:0] in_2,
  input  [1:0] rs1,
  input  in_4,
  input  [1:0] rd_add,
  input  [3:0] in_6,
  input  [1:0] rs2
);

  wire clock_1_out, decoder_1_out0, decoder_1_out1, decoder_1_out2, decoder_1_out3;
  wire [3:0] register_1_q, register_2_q, register_3_q, register_4_q;

  Decoder #(.select(2)) decoder_1 (
    .out0(decoder_1_out0), .out1(decoder_1_out1), .out2(decoder_1_out2), .out3(decoder_1_out3), .sel(rd_add),
    .en(in_4));
  Clock clock_1 (.out(clock_1_out));
  Register #(.width(4)) register_1 (.D(data), .en(decoder_1_out0), .Q(register_1_q), .clk(clock_1_out));  // open: clr
  Register #(.width(4)) register_2 (.D(data), .en(decoder_1_out1), .Q(register_2_q), .clk(clock_1_out));  // open: clr
  Register #(.width(4)) register_3 (.D(data), .en(decoder_1_out2), .Q(register_3_q), .clk(clock_1_out));  // open: clr
  Register #(.width(4)) register_4 (.D(data), .en(decoder_1_out3), .Q(register_4_q), .clk(clock_1_out));  // open: clr
  Multiplexer #(.select(2), .width(4), .enable("false")) multiplexer_1 (
    .in0(register_1_q), .in1(register_2_q), .in2(register_3_q), .in3(register_4_q), .out(in_2), .sel(rs1));
  Multiplexer #(.select(2), .width(4), .enable("false")) multiplexer_2 (
    .in0(register_1_q), .in1(register_2_q), .in2(register_3_q), .in3(register_4_q), .out(in_6), .sel(rs2));
endmodule

module alu (
  input  in_1,
  input  [11:0] in_2,
  input  [11:0] in_3,
  input  [2:0] in_4,
  output [11:0] out_5
);

  wire [11:0] adder_1_out, and_1_out, not_1_out, or_1_out, subtractor_1_out, xor_1_out;

  Adder #(.width(12)) adder_1 (.a(in_2), .b(in_3), .out(adder_1_out), .cin(in_1));  // open: cout
  Subtractor #(.width(12)) subtractor_1 (.a(in_2), .b(in_3), .out(subtractor_1_out));  // open: bin, bout
  assign and_1_out = in_2 & in_3;  // AND_Gate and_1, 12 bits wide
  assign or_1_out = in_2 | in_3;  // OR_Gate or_1, 12 bits wide
  assign xor_1_out = in_2 ^ in_3;  // XOR_Gate xor_1, 12 bits wide
  assign not_1_out = ~in_2;  // NOT_Gate not_1, 12 bits wide
  Multiplexer #(.select(3), .width(12)) multiplexer_1 (
    .in0(adder_1_out), .in1(subtractor_1_out), .in2(and_1_out), .in3(or_1_out), .in4(xor_1_out),
    .in5(not_1_out), .out(out_5), .sel(in_4));  // open: in6, in7, en
endmodule

module memory (
  input  [7:0] in_1,
  input  in_2,
  input  [11:0] in_3,
  input  in_4,
  input  in_5,
  input  in_6,
  output [11:0] out_7
);

  RAM #(.dataWidth(12), .bus("separate")) ram_1 (
    .addr(in_1), .din(in_3), .data(out_7), .str(in_2), .sel(in_4), .clk(in_6), .ld(in_5));  // open: clr
endmodule

module control_unit (
  input  [3:0] in_1,
  output R_format,
  output Load,
  output Store,
  output Branch,
  output I_Type,
  output JALR,
  output JAL,
  output LUI
);

  wire comparator_9_eq, comparator_10_eq;
  wire [3:0] undriven, undriven_2, undriven_3, undriven_4;

  Comparator #(.width(4), .mode("unsigned")) comparator_1 (.a(in_1), .b(4'b0000), .eq(R_format));  // open: gt, lt
  Comparator #(.width(4), .mode("unsigned")) comparator_2 (.a(4'b0000), .b(in_1), .eq(Load));  // open: gt, lt
  Comparator #(.width(4), .mode("unsigned")) comparator_3 (.a(4'b0000), .b(in_1), .eq(Store));  // open: gt, lt
  Comparator #(.width(4), .mode("unsigned")) comparator_4 (.a(4'b0000), .b(in_1));  // open: gt, eq, lt
  Comparator #(.width(4), .mode("unsigned")) comparator_5 (.a(4'b0000), .b(in_1), .eq(I_Type));  // open: gt, lt
  Comparator #(.width(4), .mode("unsigned")) comparator_6 (.a(undriven), .b(in_1), .eq(JALR));  // open: gt, lt
  Comparator #(.width(4), .mode("unsigned")) comparator_7 (.b(in_1), .eq(JAL));  // open: a, gt, lt
  Comparator #(.width(4), .mode("unsigned")) comparator_8 (.a(undriven_2), .b(in_1), .eq(LUI));  // open: gt, lt
  Comparator #(.width(4)) comparator_9 (.a(undriven_3), .b(in_1), .eq(comparator_9_eq));  // open: gt, lt
  Comparator #(.width(4)) comparator_10 (.a(undriven_4), .b(in_1), .eq(comparator_10_eq));  // open: gt, lt

  // Notes on the sheet:
  //   opcode
endmodule
